# Fritzing sketch CircuitoTeimosinha (saved by Fritzing 0.9.2b)

parts:
  SERVO1 = Tower Pro SG90 servo [part_number=101246]
  S1 = Toggle Switch [package=THT]
  Componente1 = Arduino Uno (Rev3)

nets:
  N1: SERVO1.Signal, Componente1.D9_PWM
  +5V: SERVO1.+5V, Componente1.5V
  GND: SERVO1.GND, S1.L1, Componente1.GND
  N2: S1.COM, Componente1.D13/SCK

notes:
  9
  13

custom parts:
  Tower Pro SG90 servo: Original file by John De Cristofaro http://www.adafruit.com/products/1449 Adafruit Feedback Servo (Small) Edited by: e-radionica.com 28/9/2015
